# Fritzing sketch Final ground (saved by Fritzing 0.9.2b)

parts:
  U1 = 2.4GHz Low Power Transceiver [package=qfn20]
  Part1 = Arduino Uno (Rev3)
  CALIB = Pushbutton [package=THT]
  RESET = Pushbutton [package=THT]
  TRIG = Pushbutton [package=THT]
  LED1 = RGB LED (com. anode, rbg) [package="5 mm [THT]"]
  R2 = Resistor [tolerance=±5% resistance=220 package="1206 [SMD]"]
  R3 = Resistor [tolerance=±5% resistance=220 package="1206 [SMD]"]
  R4 = Resistor [tolerance=±5% resistance=220 package="1206 [SMD]"]
  BATTERY = BC9VPC [package=bc9vpc]

nets:
  VSS: U1.VSS, Part1.GND, CALIB.leg0, RESET.leg0, TRIG.leg0, LED1.common_anode, BATTERY.V-
  N1: U1.CE, Part1.D7
  N2: U1.CSN, Part1.D8
  N3: U1.SCK, Part1.D13/SCK
  N4: U1.MOSI, Part1.D11_PWM/MOSI
  N5: U1.MISO, Part1.D12/MISO
  VDD: U1.VDD, Part1.3V3
  N6: Part1.A0, TRIG.leg1
  N7: Part1.A1, RESET.leg1
  N8: Part1.A2, CALIB.leg1
  N9: Part1.D3_PWM, R3.Pin_0
  N10: Part1.D5_PWM, R4.Pin_0
  N11: Part1.D6_PWM, R2.Pin_0
  N12: Part1.VIN, BATTERY.V+
  N13: LED1.red_cathode, R2.Pin_1
  N14: LED1.blue_cathode, R3.Pin_1
  N15: LED1.green_cathode, R4.Pin_1
