# Fritzing sketch Final sky (saved by Fritzing 0.9.2b)

parts:
  U1 = 2.4GHz Low Power Transceiver [package=qfn20]
  BATTERY = BC9VPC [package=bc9vpc]
  Part2 = Barometric Pressure Sensor - BMP085 Breakout
  J1 = Basic Servo
  Part1 = Arduino Uno (Rev3)

nets:
  GND: U1.VSS, BATTERY.V-, Part2.GND, J1.gnd, Part1.GND
  N1: U1.CE, Part1.D7
  N2: U1.CSN, Part1.D8
  N3: U1.SCK, Part1.D13/SCK
  N4: U1.MOSI, Part1.D11_PWM/MOSI
  N5: U1.MISO, Part1.D12/MISO
  VDD: U1.VDD, Part1.3V3
  N6: BATTERY.V+, Part1.VIN
  N7: Part2.VCC, Part1.D4
  N8: Part2.SCL, Part1.A5/SCL
  N9: Part2.SDA, Part1.A4/SDA
  VCC: J1.vcc, Part1.5V
  N10: J1.pulse, Part1.D5_PWM
